# Fritzing sketch backpack_power (saved by Fritzing 0.9.2b)

parts:
  Part1 = Arduino Uno (Rev3)
  Part2 = Arduino Pro Mini v13
  NEOPIXEL1 = Neopixel Strip -- White (30/m)
  JACK1 = 2.1mm Barrel Jack with Terminal Block

nets:
  N1: Part1.A4/SDA, Part2.A5
  N2: Part1.A5/SCL, Part2.A4
  N3: Part1.5V, Part2.RAW
  GND: Part1.GND, Part2.GND, NEOPIXEL1.GND, JACK1.NEG
  N4: Part2.D6_PWM, NEOPIXEL1.Din
  N5: NEOPIXEL1.+5V, JACK1.POS

custom parts:
  Neopixel Strip -- White (30/m): These NeoPixel strips have 30 digitally-addressable pixel LEDs per meter and are very affordable and are only 12.5 mm wide, 10 mm if you remove the strip from the casing.
